# Fritzing sketch Circuit (saved by Fritzing 0.9.4)
breadboards: 1

parts:
  Raspberry_Pi_1 = Raspberry Pi 3 [part_number=RPI-3-V1.2]
  Part1 = MQ-3 breakout
  Part2 = Logic Level Converter
  Part3 = Adafruit ADS1115 16Bit I2C ADC [part_number="Adafruit #1085"]

nets:
  N1: Raspberry_Pi_1.GPIO2, Part3.SDA
  N2: Raspberry_Pi_1.GPIO3, Part3.SCL
  GND: Raspberry_Pi_1.GND, Part1.GND, Part2.GND, Part3.AIN3, Part3.AIN2, Part3.AIN1, Part3.GND
  5V: Raspberry_Pi_1.5V, Part1.VCC, Part2.LV, Part2.HV, Part3.VDD
  N3: Part1.AO, Part2.TX2_HV
  N4: Part2.TX2_LV, Part3.AIN0

custom parts:
  MQ-3 breakout: Alcohol sensor is capable of detecting alcohol (ethanol) particles on itself and gives the information in digital form back to us to manipulate with it. SKU:101251 • Voltage: 5V DC • Power: max 750mW • Measurement range: 0.04-4mg/L
  Adafruit ADS1115 16Bit I2C ADC: For microcontrollers without an analog-to-digital converter or when you want a higher-precision ADC, the ADS1115 provides 16-bit precision at 860 samples/second over I2C. The chip can be configured as 4 single-ended input channels, or two differential channels. As a nice bonus, it even includes a programmable gain amplifier, up to x16, to help boost up smaller single/differential signals to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
